# Fritzing sketch spotmicroai (saved by Fritzing 0.9.10b)

parts:
  Mod1 = Raspberry Pi 4B
  PWM1 = PCA9685_16x12_bit_PWM_Breakout

nets:
  N1: Mod1.3V3, PWM1.connector505
  N2: Mod1.GPIO2, PWM1.connector504
  N3: Mod1.GPIO3, PWM1.connector503
  N4: Mod1.GND, PWM1.connector501
